# Fritzing sketch Schematik (saved by Fritzing 0.9.3b)
breadboards: 2

parts:
  Bauteil1 = Arduino Uno (Rev3)
  IC1 = H-Bridge [package=THT]
  S1 = Pushbutton [package="[THT]"]
  R1 = Resistor [tolerance=±5% resistance=220 package=THT]
  hc-sr1 = hc-sr04
  hc-sr2 = hc-sr04
  hc-sr3 = hc-sr04
  M1 = DC Motor
  M2 = DC Motor
  VCC1 = Battery block 9V
  LED1 = RGB LED (com. cathode, rgb) [package="5 mm [THT]"]
  LED2 = LED - 5mm [color="Orange (620nm)" package="5 mm [THT]"]
  LED3 = LED - 5mm [color="Orange (620nm)" package="5 mm [THT]"]

nets:
  N1: Bauteil1.A0, S1.Pin_1, S1.Pin_2, R1.Pin_1
  N2: Bauteil1.A1, LED1.red_anode
  N3: Bauteil1.A2, LED3.anode
  N4: Bauteil1.A3, LED2.anode
  N5: Bauteil1.A5/SCL, LED1.green_anode
  N6: Bauteil1.D8, hc-sr3.Echo
  N7: Bauteil1.D9_PWM, hc-sr1.Echo
  N8: Bauteil1.D10_PWM/SS, IC1.2A
  N9: Bauteil1.D11_PWM/MOSI, IC1.1A
  N10: Bauteil1.D12/MISO, IC1.1_2EN
  N11: Bauteil1.D13/SCK, hc-sr2.Trig
  GND: Bauteil1.GND, IC1.GND3, IC1.GND4, R1.Pin_0, hc-sr3.GND, LED1.common_cathode, LED2.cathode, LED3.cathode
  N12: Bauteil1.D2, hc-sr1.Trig
  N13: Bauteil1.D3_PWM, IC1.4A
  N14: Bauteil1.D4, hc-sr2.Echo
  N15: Bauteil1.D5_PWM, IC1.3A
  N16: Bauteil1.D6_PWM, IC1.3_4EN
  N17: Bauteil1.D7, hc-sr3.Trig
  VCC: Bauteil1.5V, IC1.VCC1, S1.Pin_3, S1.Pin_4, hc-sr1.VCC, hc-sr2.VCC, hc-sr3.VCC
  N18: IC1.1Y, M2.pin_2
  GND1: IC1.GND1, IC1.GND2, VCC1.-
  N19: IC1.2Y, M2.pin_1
  N20: IC1.VCC2, VCC1.+
  N21: IC1.3Y, M1.pin_2
  N22: IC1.4Y, M1.pin_1
